# Fritzing sketch IoT project (saved by Fritzing 0.9.6b)

parts:
  L298N1 = L298N DC motor driver
  VCC1 = Battery  # not connected
  M1 = fc-51 [package=THT]
  M2 = fc-51 [package=THT]
  M3 = fc-51 [package=THT]
  Part1 = Arduino Nano (Rev3.0) (ICSP)
  M4 = DC Motor  # not connected
  M5 = DC Motor  # not connected
  LED1 = RGB LED (com. cathode, rgb) [package="5 mm [THT]"]
  HC-SR04_Sensor_1 = HC-SR04 Ultrasonic Distance Sensor
  S1 = Pushbutton [part_number=COM-09190 package="[THT]"]
  R1 = Resistor [tolerance=±5% power=0.25 resistance=220 package=THT]
  R2 = Resistor [tolerance=±5% power=0.25 resistance=220 package=THT]
  R3 = Resistor [tolerance=±5% power=0.25 resistance=220 package=THT]
  R4 = Resistor [tolerance=±5% power=0.25 resistance=10k package=THT]

nets:
  N1: L298N1.ENA, Part1.A0
  N2: L298N1.ENB, Part1.A1
  N3: L298N1.IN1, Part1.D2
  N4: L298N1.IN2, Part1.D3
  N5: L298N1.IN3, Part1.D4
  N6: L298N1.IN4, Part1.D5
  N7: M1.pin1, Part1.D8
  N8: M2.pin1, Part1.D6
  N9: M2.pin2, Part1.GND, LED1.common_cathode
  N10: M2.pin3, Part1.VIN
  N11: M3.pin1, Part1.D7
  N12: Part1.D11/MOSI, HC-SR04_Sensor_1.TRIG
  N13: Part1.D12/MISO, HC-SR04_Sensor_1.ECHO
  N14: Part1.A5, S1.Pin_1, S1.Pin_2, R4.Pin_1
  N15: Part1.A4, R1.Pin_1
  N16: Part1.A3, R3.Pin_1
  N17: Part1.A2, R2.Pin_1

notes:
  red
  blue

custom parts:
  L298N DC motor driver: 2x DC motor driver with 78M05 positive voltage regulator (7..35 V) L298N: max 46 V, 2 A Set 5 V Enable jumper to enable 5 V regultor (needed for the L298N) and +5 V output at screw terminal or supply external +5 V at screw terminal Set ENA and/or ENB to +5 V to enable motor permanently or supply ENA and/or ENB with PWM signal IN1 and IN2 set rotation directory for motor A (OUT1/OUT2) IN2 and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
  Pushbutton: A generic pushbutton. This is a standard 12mm square momentary button. What we really like is the large button head and good tactile feel (it ‘clicks’ really well). This button is great for user input on a PCB or a good, big reset button on a breadboard. Breadboard friendly! SparkFun Storefront SKU: COM-09190 Modified by: Ho Yun "Bobby" Chan @ SparkFun Electronics Inc.
